// Digital circuit AddressDecodingLogic.dig as structural Verilog
module AddressDecodingLogic (
  input  PHI2,
  input  A15,
  input  A14,
  output CS,
  output OE,
  output CS_2,
  output OE_2,
  output CE
);

  nand nand_1 (CE, A15, A15);
  nand nand_2 (CS, PHI2, CE);
  nand nand_3 (CS_2, CE, A14);

  assign OE = A14;
  assign OE_2 = CE;

  // Notes on the sheet:
  //   RAM
  //   ROM
  //   I/O (6522, 6551)
endmodule
