// Digital circuit Test_AddressDecodingLogic.dig as structural Verilog
module Test_AddressDecodingLogic (
  input  PHI2,
  input  [15:0] ADDR,
  output CS,
  output OE,
  output CS_2,
  output OE_2,
  output CE
);

  // Probe on ADDR[15]
  // Probe on ADDR[14]
  // Probe on ADDR[13:4]
  // Probe on ADDR[3]
  // Probe on ADDR[2]
  // Probe on ADDR[1]
  // Probe on ADDR[0]
  nand nand_1 (CE, ADDR[15], ADDR[15]);
  nand nand_2 (CS, PHI2, CE);
  nand nand_3 (CS_2, CE, ADDR[14]);

  assign OE = ADDR[14];
  assign OE_2 = CE;

  // Notes on the sheet:
  //   RAM
  //   ROM
  //   I/O (6522, 6551)
endmodule
